# Fritzing sketch Pavlovbot (saved by Fritzing 0.9.3b)

parts:
  Raspberry_Pi_1 = Raspberry Pi 3 [part_number=RPI-3-V1.2]
  U1 = TRANSCHIPTC5747 [package=camera_sfv24r-2st_2]  # not connected
  R1 = Photocell (LDR) [package=THT]
  IR1 = TSOP312.., 314.. [package=THT]
  J1 = Basic Servo

nets:
  N1: Raspberry_Pi_1.3v3, IR1.Vs
  GND: Raspberry_Pi_1.GND, IR1.GND, J1.gnd
  N2: Raspberry_Pi_1.GIPO17, J1.pulse
  N3: Raspberry_Pi_1.GIPO21, IR1.Data
  N4: Raspberry_Pi_1.GIPO20, R1.pin_1
  5V: Raspberry_Pi_1.5V, R1.pin_0, J1.vcc
