# Fritzing sketch ambiente (saved by Fritzing 0.9.3b)
breadboards: 1

parts:
  S1 = Toggle Switch [package=THT]
  S2 = Toggle Switch [package=THT]
  S3 = Toggle Switch [package=THT]
  LED1 = LED - 5mm [color="Green (570nm)" package="5 mm [THT]"]
  LED2 = LED - 5mm [color="Blue (470nm)" package="5 mm [THT]"]
  LED3 = LED - 5mm [color="White (4500K)" package="5 mm [THT]"]
  Componente1 = Arduino Uno (Rev3)

nets:
  N1: S1.L1, S2.L1, S3.L1, Componente1.GND
  N2: S1.L2, LED1.cathode
  N3: S2.L2, LED2.cathode
  N4: S3.L2, LED3.cathode
  N5: LED1.anode, Componente1.D13/SCK
  N6: LED2.anode, Componente1.D12/MISO
  N7: LED3.anode, Componente1.D11_PWM/MOSI
